// Logisim project test.circ as structural Verilog: 3 circuits, main circuit Partie 1 | D.A
module Partie_1___D_A (
  input  A,
  input  B,
  output Retenue,
  output Somme
);

  and and_1 (Retenue, A, B);
  xor xor_1 (Somme, A, B);
endmodule

module Partie_2___additionneur_1_bit (
  input  A,
  input  B,
  input  Re,
  output S,
  output Rs
);

  wire and_1_out, and_2_out, xor_1_out;

  xor xor_1 (xor_1_out, A, B);
  xor xor_2 (S, xor_1_out, Re);
  and and_1 (and_1_out, Re, xor_1_out);
  and and_2 (and_2_out, B, A);
  or or_1 (Rs, and_1_out, and_2_out);
endmodule

module Partie_3___additionneur_2_bits (
  input  re,
  input  a0,
  input  a1,
  input  b0,
  input  b1,
  output rs,
  output s0,
  output s1
);
endmodule
